# Fritzing sketch Scematics (saved by Fritzing 0.9.3b)
breadboards: 1

parts:
  U1 = ESP8266 NodeMCU LoLin module
  J1 = Piezo Speaker
  LED2 = smd LED [color="Red (633nm)" package="0805 [SMD]"]
  SW-1 = Vibration sensor module

nets:
  N1: U1.D1, J1.pin2
  N2: U1.D2, SW-1.Digital_output
  3V3: U1.3V3, SW-1.vcc
  N3: U1.GND, J1.pin1, LED2.anode, SW-1.Ground
  N4: U1.D7, LED2.cathode

custom parts:
  ESP8266 NodeMCU LoLin module: ESP8266 based NodeMCU
  Vibration sensor module: Single-roller type full induction trigger switch. When no vibration or tilt, the product is ON conduction state, and in the steady state, when a vibration or tilt, the switch will be rendered instantly disconnect the conductive resistance increases, generating a current pulse signal, thereby triggering circuit. The default state of the swith is close Digital output Supply voltage:3.3V-5V On-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
